# Fritzing sketch driver (saved by Fritzing 0.9.3b)
circuit board: 2.20403cm x 3.46633cm
breadboards: 1

parts:
  R1 = Resistor [tolerance=±5% resistance=120 package=THT]
  -5V+ = female pin header, 2 pins [form="♀ (female)"]
  -12V+ = female pin header, 2 pins [form="♀ (female)"]
  S2 = female pin header, 2 pins [form="♀ (female)"]  # not connected
  S1 = female pin header, 2 pins [form="♀ (female)"]  # not connected
  LEDC = Header 3 [package=molex-1x3_lock]
  MAX485 = MAX485 [package=dil08]
  RJ45 = RJ45 Jack [package=rj45-8]

nets:
  N1: R1.Pin_0, MAX485.B, RJ45.2
  N2: R1.Pin_1, MAX485.A, RJ45.1
  N3: -5V+.pin2, LEDC.1, MAX485.RE, MAX485.DE, MAX485.VCC
  N4: -12V+.pin1, RJ45.3, RJ45.5, RJ45.7
  N5: -12V+.pin2, RJ45.4, RJ45.6, RJ45.8
  N6: LEDC.3, MAX485.DI

notes:
  Extension
  ©CC-by
  T. Theuer
  DO NOT CONNECT
  TO NETWORK
  git.io/vwEQP
  WS2812
  synyx.de
