# Fritzing sketch receiver (saved by Fritzing 0.9.3b)
circuit board: 2.38923cm x 3.60653cm
breadboards: 1

parts:
  MAX485 = MAX485 [package=dil08]
  R-7850 = Voltage Regulator - 5V [package="TO220 [THT]"]
  LED = Header 3 [package=molex-1x3_lock]
  R2 = Resistor [tolerance=±5% resistance=1k package=THT]
  R1 = Resistor [tolerance=±5% resistance=120 package=THT]
  R3 = Resistor [tolerance=±5% resistance=1k package=THT]
  R4 = Resistor [tolerance=±5% resistance=470 package=THT]
  RJ45 = RJ45 Jack [package=rj45-8]

nets:
  N1: MAX485.RO, R4.Pin_0
  N2: MAX485.A, R1.Pin_1, R3.Pin_0, RJ45.1
  N3: MAX485.B, R2.Pin_1, R1.Pin_0, RJ45.2
  N4: MAX485.VCC, R-7850.output_voltage, LED.1, R3.Pin_1
  N5: R-7850.input_voltage, RJ45.4, RJ45.6, RJ45.8
  N6: LED.3, R4.Pin_1

notes:
  WS2812
  Extension
  ©CC-by
  T. Theuer
  DO NOT CONNECT
  TO NETWORK
  git.io/vwEQP
  synyx.de
