# Fritzing sketch receiver_deprecated (saved by Fritzing 0.9.2b)
circuit board: 2.13382cm x 3.5549cm
breadboards: 1

parts:
  RJ45 = RJ45 Jack [package=rj45-8]
  MAX485 = MAX485 [package=dil08]
  R1 = Resistor [tolerance=±5% resistance=120 package=THT]
  R2 = Resistor [tolerance=±5% resistance=470 package=THT]
  R3 = Resistor [tolerance=±5% resistance=470 package=THT]
  LED = Header 3 [package=molex-1x3_lock]
  R-7850 = Voltage Regulator - 5V [package="TO220 [THT]"]
  R4 = Resistor [package=THT]

nets:
  N1: RJ45.1, MAX485.A, R1.Pin_0, R3.Pin_1
  N2: RJ45.2, MAX485.B, R1.Pin_1, R2.Pin_1
  N3: RJ45.4, RJ45.6, RJ45.8, R-7850.input_voltage
  N4: MAX485.RO, R4.pin_0
  N5: MAX485.VCC, R2.Pin_0, LED.1, R-7850.output_voltage
  N6: LED.3, R4.pin_1

custom parts:
  Resistor: A generic resistor
