# Fritzing sketch unified thing (saved by Fritzing 0.9.2b)
breadboards: 1

parts:
  RJ45 = RJ45 Jack [package=rj45-8]
  MAX485 = MAX485 [package=dil08]
  R1 = Resistor [tolerance=±5% resistance=120 package=THT]
  VCC1 = Battery

nets:
  N1: RJ45.1, MAX485.A, R1.Pin_1
  N2: RJ45.2, MAX485.B, R1.Pin_0
  N3: MAX485.RE, MAX485.DE
  N4: MAX485.GND, VCC1.-
  N5: MAX485.VCC, VCC1.+
